// Logisim project index.circ as structural Verilog
module HA (
  input  A,
  input  B,
  output sum,
  output carry
);

  xor xor_1 (sum, A, B);
  and and_1 (carry, A, B);
endmodule

module FullAdder (
  input  Cin,
  input  A,
  input  B,
  output Sum,
  output Cout
);

  wire ha_1_carry, ha_1_sum, ha_2_carry;

  HA ha_1 (.A(A), .B(B), .sum(ha_1_sum), .carry(ha_1_carry));
  HA ha_2 (.A(Cin), .B(ha_1_sum), .sum(Sum), .carry(ha_2_carry));
  xor xor_1 (Cout, ha_2_carry, ha_1_carry);
endmodule
